// Logisim project IT012_LAB01_25520646.circ as structural Verilog: 5 circuits, main circuit Warmup
module Warmup (
  input  A,
  input  B,
  output F
);

  wire not_1_out;

  not not_1 (not_1_out, B);
  and and_1 (F, A, not_1_out);
endmodule

module TN1 (
  input  A,
  input  B,
  input  C,
  output out_4,
  output out_5,
  output XOR3,
  output out_7,
  output NAND3,
  output out_9,
  output out_10,
  output out_11,
  output CHAIN,
  output out_13
);

  wire X_out;

  not not_1 (out_4, A);
  and and_1 (out_5, A, B);
  or or_1 (out_7, A, B);
  nand nand_1 (out_9, A, B);
  nor nor_1 (out_10, A, B);
  xor xor_1 (out_11, A, B);
  xnor xnor_1 (out_13, A, B);
  xor xor_2 (XOR3, A, B, C);
  nand nand_2 (NAND3, A, B, C);
  nand X (X_out, A, B);
  nand nand_3 (CHAIN, X_out, C);
endmodule

module TN2 (
  input  X,
  input  Y,
  input  Z,
  output EQ1,
  output EQ2,
  output EQ3,
  output EQ4,
  output EQ5
);

  wire and_1_out, and_2_out, and_3_out, and_4_out, and_5_out, not_1_out, not_2_out, not_3_out, not_4_out,
       not_5_out, or_1_out, or_2_out, or_3_out, or_4_out, or_5_out, or_6_out;

  and and_1 (and_1_out, Y, Z);
  not not_1 (not_1_out, X);
  and and_2 (and_2_out, X, Y);
  or or_1 (or_1_out, and_1_out, X);
  and and_3 (and_3_out, not_1_out, Y);
  or or_2 (or_2_out, X, Y);
  not not_2 (not_2_out, and_2_out);
  or or_3 (or_3_out, and_3_out, X);
  not not_3 (not_3_out, or_2_out);
  xnor xnor_1 (EQ1, not_3_out, and_4_out);
  xnor xnor_2 (EQ2, not_2_out, and_4_out);
  xnor xnor_3 (EQ3, or_1_out, and_5_out);
  xnor xnor_4 (EQ4, or_3_out, X);
  xnor xnor_5 (EQ5, or_3_out, or_4_out);
  and and_4 (and_4_out, not_4_out, not_5_out);
  not not_4 (not_4_out, X);
  not not_5 (not_5_out, Y);
  and and_5 (and_5_out, or_5_out, or_6_out);
  or or_4 (or_4_out, X, Y);
  or or_5 (or_5_out, X, Y);
  or or_6 (or_6_out, X, Z);
endmodule

module TN3 (
  input  A,
  input  B,
  input  C,
  input  D,
  output F
);

  wire and_1_out, and_2_out, and_3_out, and_4_out, and_5_out, and_6_out, not_1_out, not_2_out, not_3_out,
       not_4_out, not_5_out, not_6_out, not_7_out, not_8_out, not_9_out, not_10_out;

  not not_1 (not_1_out, A);
  not not_2 (not_2_out, C);
  not not_3 (not_3_out, A);
  not not_4 (not_4_out, B);
  not not_5 (not_5_out, A);
  not not_6 (not_6_out, B);
  and and_1 (and_1_out, not_5_out, not_6_out, C, not_7_out);
  not not_7 (not_7_out, D);
  not not_8 (not_8_out, A);
  not not_9 (not_9_out, B);
  and and_2 (and_2_out, not_8_out, not_9_out, C, D);
  and and_3 (and_3_out, not_1_out, B, not_2_out, D);
  and and_4 (and_4_out, not_3_out, B, C, D);
  and and_5 (and_5_out, A, not_4_out, C, D);
  and and_6 (and_6_out, A, B, not_10_out, D);
  not not_10 (not_10_out, C);
  or or_1 (F, and_1_out, and_2_out, and_3_out, and_4_out, and_5_out, and_6_out);
endmodule

module TN4 (
  input  A,
  input  B,
  input  C,
  input  D,
  output F_can,
  output EQ1,
  output F_sop,
  output EQ2,
  output F_pos
);

  wire and_1_out, and_2_out, and_3_out, and_4_out, and_5_out, and_6_out, and_7_out, and_8_out, and_9_out,
       and_10_out, not_1_out, not_2_out, not_3_out, not_4_out, not_5_out, not_6_out, not_7_out, not_8_out,
       not_9_out, not_10_out, not_11_out, not_12_out, not_13_out, not_14_out, not_15_out, not_16_out,
       not_17_out, not_18_out, not_19_out, not_20_out, not_21_out, not_22_out, or_1_out, or_2_out, or_3_out,
       or_4_out, or_5_out;

  not not_1 (not_1_out, A);
  not not_2 (not_2_out, B);
  not not_3 (not_3_out, A);
  not not_4 (not_4_out, C);
  not not_5 (not_5_out, B);
  not not_6 (not_6_out, B);
  not not_7 (not_7_out, C);
  not not_8 (not_8_out, A);
  not not_9 (not_9_out, B);
  not not_10 (not_10_out, C);
  not not_11 (not_11_out, A);
  not not_12 (not_12_out, C);
  and and_1 (and_1_out, not_1_out, not_2_out, C);
  and and_2 (and_2_out, not_3_out, B, D);
  and and_3 (and_3_out, B, not_4_out, D);
  and and_4 (and_4_out, not_5_out, C, D);
  or or_1 (or_1_out, C, D);
  or or_2 (or_2_out, B, C);
  or or_3 (or_3_out, not_6_out, not_7_out, D);
  or or_4 (or_4_out, not_8_out, not_9_out, not_10_out);
  or or_5 (or_5_out, not_11_out, not_12_out, D);
  not not_13 (not_13_out, A);
  not not_14 (not_14_out, C);
  not not_15 (not_15_out, A);
  not not_16 (not_16_out, B);
  not not_17 (not_17_out, A);
  not not_18 (not_18_out, B);
  and and_5 (and_5_out, not_17_out, not_18_out, C, not_19_out);
  not not_19 (not_19_out, D);
  not not_20 (not_20_out, A);
  not not_21 (not_21_out, B);
  and and_6 (and_6_out, not_20_out, not_21_out, C, D);
  and and_7 (and_7_out, not_13_out, B, not_14_out, D);
  and and_8 (and_8_out, not_15_out, B, C, D);
  and and_9 (and_9_out, A, not_16_out, C, D);
  and and_10 (and_10_out, A, B, not_22_out, D);
  not not_22 (not_22_out, C);
  or or_6 (F_sop, and_1_out, and_2_out, and_3_out, and_4_out);
  and and_11 (F_pos, or_1_out, or_2_out, or_3_out, or_4_out, or_5_out);
  or or_7 (F_can, and_5_out, and_6_out, and_7_out, and_8_out, and_9_out, and_10_out);
  xnor xnor_1 (EQ1, F_can, F_sop);
  xnor xnor_2 (EQ2, F_can, F_pos);
endmodule
